# Fritzing sketch Untitled Sketch 2 (saved by Fritzing 0.9.3b)

parts:
  U1 = ESP8266 NodeMCU LoLin module
  Part1 = RFID-RC522-v2

nets:
  N1: U1.D3, Part1.RST
  N2: U1.D4, Part1.SDA
  3V3: U1.3V3, Part1.3.3V
  N3: U1.D5, Part1.SCK
  N4: U1.D6, Part1.MISO
  N5: U1.D7, Part1.MOSI
  GND: U1.GND, Part1.GND

notes:
  SDA - D4
  DCK - D5
  MOSI - D7
  MISO - D6
  GND - GND
  RST - D3
  3V - 3.3V

custom parts:
  ESP8266 NodeMCU LoLin module: ESP8266 based NodeMCU
  RFID-RC522-v2: A simple China made RFID-RC522 Reader; do check the pin labels, as this is a MFRC522 based clone.
